# Fritzing sketch Jupiter_Pir (saved by Fritzing 0.9.2b)
circuit board: 8.46667cm x 5.64444cm
breadboards: 1

parts:
  Composant1 = Arduino Uno (Rev3)
  PIR1 = PIR sensor
  R1 = Resistor [tolerance=±5% resistance=10k package=THT]
  LED1 = LED - 5mm [color="Red (633nm)" package="5 mm [THT]"]
  PIR2 = PIR sensor
  R2 = Resistor [tolerance=±5% resistance=10k package=THT]
  S1 = Pushbutton [package="[THT]"]
  R3 = Resistor [tolerance=±5% resistance=10k package=THT]

nets:
  N1: Composant1.D13/SCK, LED1.anode
  GND: Composant1.GND, PIR1.GND, LED1.cathode, PIR2.GND, R3.Pin_0
  N2: Composant1.D2, PIR1.SIG, R1.Pin_0
  N3: Composant1.D3_PWM, PIR2.SIG, R2.Pin_0
  N4: Composant1.D7, S1.Pin_3, S1.Pin_4, R3.Pin_1
  VDD: Composant1.5V, PIR1.VDD, R1.Pin_1, PIR2.VDD, R2.Pin_1, S1.Pin_1, S1.Pin_2
